// Logisim project Georgios.circ as structural Verilog: 7 circuits, main circuit main
module main (
  input  in_1
);

  wire Begin_out, clock_1_out, Halt_out, or_1_out, Reset_out, Step_out;
  wire [7:0] state_1_ic_out;
  wire [31:0] rom_1_data;

  Button Begin (.out(Begin_out));
  Button Halt (.out(Halt_out));
  Button Reset (.out(Reset_out));
  Button Step (.out(Step_out));
  Clock clock_1 (.out(clock_1_out));
  buf or_1 (or_1_out, Halt_out);  // OR_Gate
  State state_1 (
    .Begin(Begin_out), .Halt(or_1_out), .Reset(Reset_out), .Step(Step_out), .Clock_IN(clock_1_out),
    .IC_Enable(in_1), .IC_OUT(state_1_ic_out));  // open: IC_IN, Clock_OUT
  ROM #(.dataWidth(32)) rom_1 (.addr(state_1_ic_out), .data(rom_1_data));  // open: sel
  ALU alu_1 ();  // open: Underflow, Overflow, A, Subtract, B, Result
  Registers registers_1 ();  // open: X_SELECT, X_ENABLE, X_OUT, Y_SELECT, Y_ENABLE, Y_OUT, Z_SELECT, Z_ENABLE, Z_IN

  // Notes on the sheet:
  //   Georgios 2
endmodule

module Registers (
  input  [7:0] X_SELECT,
  input  X_ENABLE,
  input  [7:0] Y_SELECT,
  input  Y_ENABLE,
  input  [7:0] Z_SELECT,
  input  Z_ENABLE,
  input  [7:0] Z_IN,
  output [7:0] X_OUT,
  output [7:0] Y_OUT
);

  wire demultiplexer_2_out0, demultiplexer_2_out1, demultiplexer_2_out2, demultiplexer_2_out3,
       demultiplexer_2_out4, demultiplexer_2_out5, demultiplexer_2_out6, demultiplexer_2_out7,
       demultiplexer_2_out8, demultiplexer_2_out9, demultiplexer_2_out10, demultiplexer_2_out11,
       demultiplexer_2_out12, demultiplexer_2_out13, demultiplexer_2_out14, demultiplexer_2_out15;
  wire [3:0] bitselector_1_out, bitselector_2_out, bitselector_3_out;
  wire [7:0] demultiplexer_1_out0, demultiplexer_1_out1, demultiplexer_1_out2, demultiplexer_1_out3,
       demultiplexer_1_out4, demultiplexer_1_out5, demultiplexer_1_out6, demultiplexer_1_out7,
       demultiplexer_1_out8, demultiplexer_1_out9, demultiplexer_1_out10, demultiplexer_1_out11,
       demultiplexer_1_out12, demultiplexer_1_out13, demultiplexer_1_out14, demultiplexer_1_out15,
       register_1_q, register_2_q, register_3_q, register_4_q, register_5_q, register_6_q, register_7_q,
       register_8_q, register_9_q, register_10_q, register_11_q, register_12_q, register_13_q, register_14_q,
       register_15_q, register_16_q;

  Demultiplexer #(.select(4), .width(8)) demultiplexer_1 (
    .out0(demultiplexer_1_out0), .out1(demultiplexer_1_out1), .out2(demultiplexer_1_out2),
    .out3(demultiplexer_1_out3), .out4(demultiplexer_1_out4), .out5(demultiplexer_1_out5),
    .out6(demultiplexer_1_out6), .out7(demultiplexer_1_out7), .out8(demultiplexer_1_out8),
    .out9(demultiplexer_1_out9), .out10(demultiplexer_1_out10), .out11(demultiplexer_1_out11),
    .out12(demultiplexer_1_out12), .out13(demultiplexer_1_out13), .out14(demultiplexer_1_out14),
    .out15(demultiplexer_1_out15), .in(Z_IN), .sel(bitselector_1_out), .en(Z_ENABLE));
  BitSelector #(.group(4)) bitselector_1 (.in(Z_SELECT), .out(bitselector_1_out), .sel(1'b0));
  Demultiplexer #(.select(4)) demultiplexer_2 (
    .out0(demultiplexer_2_out0), .out1(demultiplexer_2_out1), .out2(demultiplexer_2_out2),
    .out3(demultiplexer_2_out3), .out4(demultiplexer_2_out4), .out5(demultiplexer_2_out5),
    .out6(demultiplexer_2_out6), .out7(demultiplexer_2_out7), .out8(demultiplexer_2_out8),
    .out9(demultiplexer_2_out9), .out10(demultiplexer_2_out10), .out11(demultiplexer_2_out11),
    .out12(demultiplexer_2_out12), .out13(demultiplexer_2_out13), .out14(demultiplexer_2_out14),
    .out15(demultiplexer_2_out15), .in(Z_ENABLE), .sel(bitselector_1_out));  // open: en
  Multiplexer #(.select(4), .width(8)) multiplexer_1 (
    .in0(register_1_q), .in1(register_2_q), .in2(register_3_q), .in3(register_4_q), .in4(register_5_q),
    .in5(register_6_q), .in6(register_7_q), .in7(register_8_q), .in8(register_9_q), .in9(register_10_q),
    .in10(register_11_q), .in11(register_12_q), .in12(register_13_q), .in13(register_14_q),
    .in14(register_15_q), .in15(register_16_q), .out(X_OUT), .sel(bitselector_2_out), .en(X_ENABLE));
  BitSelector #(.group(4)) bitselector_2 (.in(X_SELECT), .out(bitselector_2_out), .sel(1'b0));
  Register register_1 (.D(demultiplexer_1_out0), .Q(register_1_q), .clk(demultiplexer_2_out0));  // open: en, clr
  Register register_2 (.D(demultiplexer_1_out1), .Q(register_2_q), .clk(demultiplexer_2_out1));  // open: en, clr
  Register register_3 (.D(demultiplexer_1_out2), .Q(register_3_q), .clk(demultiplexer_2_out2));  // open: en, clr
  Register register_4 (.D(demultiplexer_1_out3), .Q(register_4_q), .clk(demultiplexer_2_out3));  // open: en, clr
  Register register_5 (.D(demultiplexer_1_out4), .Q(register_5_q), .clk(demultiplexer_2_out4));  // open: en, clr
  Register register_6 (.D(demultiplexer_1_out5), .Q(register_6_q), .clk(demultiplexer_2_out5));  // open: en, clr
  Register register_7 (.D(demultiplexer_1_out6), .Q(register_7_q), .clk(demultiplexer_2_out6));  // open: en, clr
  Register register_8 (.D(demultiplexer_1_out7), .Q(register_8_q), .clk(demultiplexer_2_out7));  // open: en, clr
  Multiplexer #(.select(4), .width(8)) multiplexer_2 (
    .in0(register_1_q), .in1(register_2_q), .in2(register_3_q), .in3(register_4_q), .in4(register_5_q),
    .in5(register_6_q), .in6(register_7_q), .in7(register_8_q), .in8(register_9_q), .in9(register_10_q),
    .in10(register_11_q), .in11(register_12_q), .in12(register_13_q), .in13(register_14_q),
    .in14(register_15_q), .in15(register_16_q), .out(Y_OUT), .sel(bitselector_3_out), .en(Y_ENABLE));
  BitSelector #(.group(4)) bitselector_3 (.in(Y_SELECT), .out(bitselector_3_out), .sel(1'b0));
  Register register_9 (.D(demultiplexer_1_out8), .Q(register_9_q), .clk(demultiplexer_2_out8));  // open: en, clr
  Register register_10 (.D(demultiplexer_1_out9), .Q(register_10_q), .clk(demultiplexer_2_out9));  // open: en, clr
  Register register_11 (.D(demultiplexer_1_out10), .Q(register_11_q), .clk(demultiplexer_2_out10));  // open: en, clr
  Register register_12 (.D(demultiplexer_1_out11), .Q(register_12_q), .clk(demultiplexer_2_out11));  // open: en, clr
  Register register_13 (.D(demultiplexer_1_out12), .Q(register_13_q), .clk(demultiplexer_2_out12));  // open: en, clr
  Register register_14 (.D(demultiplexer_1_out13), .Q(register_14_q), .clk(demultiplexer_2_out13));  // open: en, clr
  Register register_15 (.D(demultiplexer_1_out14), .Q(register_15_q), .clk(demultiplexer_2_out14));  // open: en, clr
  Register register_16 (.D(demultiplexer_1_out15), .Q(register_16_q), .clk(demultiplexer_2_out15));  // open: en, clr

  // Notes on the sheet:
  //   Z
  //   Register 0
  //   X
  //   Y
  //   Register F
endmodule

module ALU (
  input  [7:0] A,
  input  Subtract,
  input  [7:0] B,
  output [7:0] Result,
  output Underflow,
  output Overflow
);

  wire adder_1_cout, not_2_out, not_3_out;
  wire [7:0] multiplexer_1_out, not_1_out;

  Multiplexer #(.width(8), .enable("false")) multiplexer_1 (
    .in0(B), .in1(not_1_out), .out(multiplexer_1_out), .sel(Subtract));
  assign not_1_out = ~B;  // NOT_Gate not_1, 8 bits wide
  Adder adder_1 (.a(A), .b(multiplexer_1_out), .out(Result), .cin(Subtract), .cout(adder_1_cout));
  not not_2 (not_2_out, adder_1_cout);
  and and_1 (Underflow, not_2_out, Subtract);
  not not_3 (not_3_out, Subtract);
  and and_2 (Overflow, not_3_out, adder_1_cout);
endmodule

module Decoder (
  input  [7:0] INSTRUCTION,
  output Subtract,
  output Halt
);

  wire and_1_out, and_2_out, and_3_out, and_4_out, and_5_out, and_6_out, and_7_out, and_8_out, and_10_out,
       and_11_out, and_12_out, and_13_out, and_14_out, and_15_out, and_16_out, not_1_out, not_2_out,
       not_3_out, not_4_out, not_5_out, not_6_out, not_7_out, not_8_out, or_1_out;
  wire [3:0] bitselector_1_out;

  BitSelector #(.group(4)) bitselector_1 (.in(INSTRUCTION), .out(bitselector_1_out), .sel(1'b0));
  not not_1 (not_1_out, bitselector_1_out[3]);
  and and_1 (and_1_out, not_1_out, not_2_out);
  not not_2 (not_2_out, bitselector_1_out[2]);
  not not_3 (not_3_out, bitselector_1_out[3]);
  and and_2 (and_2_out, not_3_out, bitselector_1_out[2]);
  and and_3 (and_3_out, bitselector_1_out[3], not_4_out);
  not not_4 (not_4_out, bitselector_1_out[2]);
  and and_4 (and_4_out, bitselector_1_out[3], bitselector_1_out[2]);
  not not_5 (not_5_out, bitselector_1_out[1]);
  and and_5 (and_5_out, not_5_out, not_6_out);
  not not_6 (not_6_out, bitselector_1_out[0]);
  not not_7 (not_7_out, bitselector_1_out[1]);
  and and_6 (and_6_out, not_7_out, bitselector_1_out[0]);
  and and_7 (and_7_out, bitselector_1_out[1], not_8_out);
  not not_8 (not_8_out, bitselector_1_out[0]);
  and and_8 (and_8_out, bitselector_1_out[1], bitselector_1_out[0]);
  or or_1 (or_1_out, and_2_out, and_11_out, and_12_out);
  and and_9 (Halt, and_1_out, and_5_out);
  and and_10 (and_10_out, and_1_out, and_6_out);
  and and_11 (and_11_out, and_1_out, and_7_out);
  and and_12 (and_12_out, and_1_out, and_8_out);
  and and_13 (and_13_out, and_2_out, and_5_out);
  and and_14 (and_14_out, and_2_out, and_6_out);
  and and_15 (and_15_out, and_2_out, and_7_out);
  and and_16 (and_16_out, and_2_out, and_8_out);
endmodule

module State (
  input  Begin,
  input  Halt,
  input  Reset,
  input  Step,
  input  Clock_IN,
  input  IC_Enable,
  input  [7:0] IC_IN,
  output [7:0] IC_OUT,
  output Clock_OUT
);

  wire and_1_out, d_ff_1_q, not_1_out, not_2_out, not_3_out, not_4_out, not_5_out, or_2_out;
  wire [7:0] adder_1_out, multiplexer_1_out;

  D_Flip_Flop d_ff_1 (.Q(d_ff_1_q), .preset(Begin), .reset(Halt));  // open: clk, D, Qn, en
  Adder adder_1 (.a(IC_OUT), .b(8'h1), .out(adder_1_out));  // open: cin, cout
  or or_1 (Clock_OUT, Step, Reset, and_1_out);
  and and_1 (and_1_out, d_ff_1_q, Clock_IN);
  Multiplexer #(.width(8)) multiplexer_1 (
    .in0(adder_1_out), .in1(IC_IN), .out(multiplexer_1_out), .sel(not_2_out));  // open: en
  not not_1 (not_1_out, not_3_out);
  not not_2 (not_2_out, Clock_OUT);
  not not_3 (not_3_out, or_2_out);
  or or_2 (or_2_out, IC_Enable, Clock_OUT);
  Register register_1 (.D(multiplexer_1_out), .Q(IC_OUT), .clk(not_4_out), .clr(Reset));  // open: en
  not not_4 (not_4_out, not_5_out);
  not not_5 (not_5_out, not_1_out);
endmodule

module Router (
  input  [7:0] ALU_IN,
  input  [7:0] Register_X_IN,
  input  [7:0] ARGUMENT_1,
  input  [7:0] Register_Y_IN,
  input  [7:0] ARGUMENT_2,
  input  [7:0] ARGUMENT_3,
  input  Clock,
  output [7:0] ALU_A,
  output [7:0] ALU_B,
  output [7:0] Register_Select_X,
  output Enable_X,
  output [7:0] Register_Select_Y,
  output Enable_Y,
  output [7:0] Register_Select_Z,
  output Register_Enable_Z,
  output [7:0] Register_Set_Z
);

  wire delay_1_out_9, delay_1_out_11, delay_1_out_13, undriven, undriven_2, undriven_4, undriven_5;
  wire [1:0] undriven_3;
  wire [7:0] demultiplexer_1_out1, demultiplexer_2_out0, demultiplexer_3_out0;

  Demultiplexer #(.width(8)) demultiplexer_1 (
    .out0(Register_Select_Y), .out1(demultiplexer_1_out1), .in(ARGUMENT_3), .sel(undriven));  // open: en
  Demultiplexer #(.width(8)) demultiplexer_2 (
    .out0(demultiplexer_2_out0), .out1(Register_Select_X), .in(ARGUMENT_2), .sel(undriven_2));  // open: en
  Delay delay_1 (
    .out_9(delay_1_out_9), .in_3(delay_1_out_9), .out_11(delay_1_out_11), .in_5(delay_1_out_11),
    .out_13(delay_1_out_13), .in_7(delay_1_out_13), .out_15(Register_Enable_Z));  // open: in_1, in_2, out_10, in_4, out_12, in_6, out_14, in_8, out_16
  Multiplexer #(.width(8)) multiplexer_1 (
    .in0(Register_Y_IN), .in1(demultiplexer_1_out1), .out(ALU_B), .sel(undriven_4));  // open: en
  Demultiplexer #(.width(8)) demultiplexer_3 (
    .out0(demultiplexer_3_out0), .out1(ALU_A), .in(Register_X_IN), .sel(undriven_5));  // open: en
  Multiplexer #(.select(2), .width(8)) multiplexer_2 (
    .in0(demultiplexer_2_out0), .in1(demultiplexer_3_out0), .in2(ALU_IN), .out(Register_Set_Z),
    .sel(undriven_3));  // open: in3, en

  assign Register_Select_Z = ARGUMENT_1;

  // Notes on the sheet:
  //   $
endmodule

module Delay (
  input  in_1,
  input  in_2,
  input  in_3,
  input  in_4,
  input  in_5,
  input  in_6,
  input  in_7,
  input  in_8,
  output out_9,
  output out_10,
  output out_11,
  output out_12,
  output out_13,
  output out_14,
  output out_15,
  output out_16
);

  not not_1 (out_9, in_1);
  not not_2 (out_10, in_2);
  not not_3 (out_11, in_3);
  not not_4 (out_12, in_4);
  not not_5 (out_14, in_6);
  not not_6 (out_13, in_5);
  not not_7 (out_16, in_8);
  not not_8 (out_15, in_7);
endmodule
